// Logisim project 8 BIT HALF SUBTRACTOR.circ as structural Verilog: 1 circuit, main circuit main
module main (
  input  in_1,
  input  in_2,
  output out_3,
  output out_4
);

  wire not_1_out;

  not not_1 (not_1_out, in_1);
  xor xor_1 (out_3, in_1, in_2);
  and and_1 (out_4, not_1_out, not_1_out, in_1);

  // Notes on the sheet:
  //   8 BIT HALF SUBTRACTOR
endmodule
